// Logisim project mata3820171.circ as structural Verilog
module main (
  input  [7:0] E3,
  input  [7:0] E2,
  input  [7:0] E1,
  input  [7:0] E0,
  input  [1:0] in_5,
  input  [1:0] in_6,
  input  [7:0] in_7,
  input  [7:0] in_8,
  output [7:0] out_9,
  output [7:0] out_10,
  output [7:0] out_11,
  output [7:0] out_12,
  output [7:0] out_13,
  output [7:0] out_14,
  output [7:0] out_15,
  output [7:0] out_16,
  output [7:0] out_17,
  output [7:0] out_18,
  output [7:0] out_19,
  output [7:0] out_20,
  output [7:0] out_21,
  output [7:0] out_22,
  output [7:0] out_23,
  output [7:0] out_24,
  output [7:0] out_25,
  output [7:0] out_26,
  output [7:0] out_27,
  output [7:0] out_28,
  output [7:0] out_29,
  output [7:0] out_30,
  output [7:0] out_31,
  output [7:0] out_32,
  output [7:0] out_33,
  output [7:0] out_34,
  output [7:0] out_35,
  output [7:0] out_36,
  output [7:0] out_37,
  output [7:0] out_38,
  output [7:0] out_39,
  output [7:0] out_40,
  output [7:0] out_41,
  output [7:0] out_42,
  output [7:0] out_43,
  output [7:0] out_44,
  output [7:0] out_45,
  output [7:0] out_46,
  output [7:0] out_47,
  output [7:0] out_48,
  output [7:0] out_49,
  output [7:0] out_50,
  output [7:0] out_51,
  output [7:0] out_52,
  output [7:0] out_53,
  output [7:0] out_54,
  output [7:0] out_55
);

  wire adder_1_cout, clock_1_out, comparator_1_eq, comparator_2_lt, comparator_3_gt, comparator_4_eq,
       comparator_4_lt, comparator_5_eq, comparator_5_gt, or_1_out, or_2_out, undriven;
  wire [7:0] multiplexer_1_out, multiplexer_2_out, multiplexer_8_out;

  Clock clock_1 (.out(clock_1_out));
  Multiplexer #(.select(2), .width(8)) multiplexer_1 (
    .in0(out_12), .in1(out_11), .in2(out_10), .in3(out_9), .out(multiplexer_1_out), .sel(in_5));  // open: en
  Register R0 (.D(multiplexer_8_out), .en(undriven), .Q(out_12), .clk(clock_1_out));  // open: clr
  Register R1 (.D(E1), .Q(out_11), .clk(clock_1_out));  // open: en, clr
  Register R2 (.D(E2), .Q(out_10), .clk(clock_1_out));  // open: en, clr
  Register R3 (.D(E3), .Q(out_9), .clk(clock_1_out));  // open: en, clr
  Multiplexer #(.select(2), .width(8)) multiplexer_2 (
    .in0(out_12), .in1(out_11), .in2(out_10), .in3(out_9), .out(multiplexer_2_out), .sel(in_6));  // open: en
  Demultiplexer #(.select(4), .width(8)) demultiplexer_1 (
    .out0(out_14), .out1(out_15), .out2(out_17), .out3(out_18), .out4(out_19), .out5(out_21), .out6(out_22),
    .out7(out_24), .out8(out_25), .out9(out_26), .out10(out_28), .out11(out_29), .out12(out_30),
    .out13(out_30), .out14(out_30), .out15(out_30), .in(multiplexer_1_out), .sel(4'b1010));  // open: en
  Demultiplexer #(.select(4), .width(8)) demultiplexer_2 (
    .out0(out_36), .out1(out_38), .out2(out_39), .out3(out_40), .out4(out_41), .out5(out_42), .out6(out_44),
    .out7(out_45), .out8(out_46), .out9(out_47), .out10(out_48), .out11(out_50), .out12(out_51),
    .out13(out_52), .out14(out_54), .out15(out_55), .in(multiplexer_2_out), .sel(4'b1010));  // open: en
  Comparator #(.mode("unsigned")) comparator_1 (.a(out_22), .b(out_44), .eq(comparator_1_eq));  // open: gt, lt
  Comparator #(.mode("unsigned")) comparator_2 (.a(out_24), .b(out_45), .lt(comparator_2_lt));  // open: gt, eq
  Comparator #(.mode("unsigned")) comparator_3 (.a(out_25), .b(out_46), .gt(comparator_3_gt));  // open: eq, lt
  Comparator #(.mode("unsigned")) comparator_4 (
    .a(out_26), .b(out_47), .eq(comparator_4_eq), .lt(comparator_4_lt));  // open: gt
  Comparator #(.mode("unsigned")) comparator_5 (
    .a(out_28), .b(out_48), .gt(comparator_5_gt), .eq(comparator_5_eq));  // open: lt
  or or_1 (or_1_out, comparator_4_eq, comparator_4_lt);
  or or_2 (or_2_out, comparator_5_gt, comparator_5_eq);
  assign out_13 = out_15 & out_36;  // AND_Gate and_1, 8 bits wide
  assign out_16 = out_14 | out_38;  // OR_Gate or_3, 8 bits wide
  assign out_20 = out_17 ^ out_39;  // XOR_Gate xor_1, 8 bits wide
  assign out_23 = ~out_18;  // NOT_Gate not_1, 8 bits wide
  Adder adder_1 (.a(out_19), .b(out_41), .out(out_27), .cout(adder_1_cout));  // open: cin
  Subtractor subtractor_1 (.a(out_21), .b(out_42), .out(out_31));  // open: bin, bout
  Multiplexer #(.width(8)) multiplexer_3 (.in0(in_7), .in1(in_8), .out(out_34), .sel(comparator_1_eq));  // open: en
  Multiplexer #(.width(8)) multiplexer_4 (.in0(in_7), .in1(in_8), .out(out_37), .sel(comparator_2_lt));  // open: en
  Multiplexer #(.width(8)) multiplexer_5 (.in0(in_7), .in1(in_8), .out(out_43), .sel(comparator_3_gt));  // open: en
  Multiplexer #(.width(8)) multiplexer_6 (.in0(in_7), .in1(in_8), .out(out_49), .sel(or_1_out));  // open: en
  Multiplexer #(.width(8)) multiplexer_7 (.in0(in_7), .in1(in_8), .out(out_53), .sel(or_2_out));  // open: en
  Multiplexer #(.select(4), .width(8)) multiplexer_8 (
    .in0(out_13), .in1(out_16), .in2(out_20), .in3(out_23), .in4(out_27), .in5(out_31), .in6(out_34),
    .in7(out_37), .in8(out_43), .in9(out_49), .in10(out_53), .out(multiplexer_8_out), .sel(4'b1010));  // open: in11, in12, in13, in14, in15, en

  assign out_32 = out_30;
  assign out_33 = out_30;
  assign out_35 = out_30;

  // Notes on the sheet:
  //   Rx
  //   Ry
endmodule
